# Fritzing sketch usb_modbus (saved by Fritzing 0.9.4)

parts:
  Компонент1 = Arduino Mega 2560 (Rev3)
  MODBUS = RS485 Module (MAX3485)
  DMX = RS485 Module (MAX3485)
  LED1 = smd LED [color="Red (633nm)" package="0603 [SMD]"]
  J1 = Screw terminal - 2 pins [package=THT]
  J2 = Screw terminal - 2 pins [package=THT]

nets:
  N1: Компонент1.D21/SCL, LED1.anode
  N2: Компонент1.D19/RX1, DMX.RO
  N3: Компонент1.D18/TX1, DMX.DI
  N4: Компонент1.D17_PWM/RX2, MODBUS.RO
  N5: Компонент1.D16_PWM/TX2, MODBUS.DI
  GND: Компонент1.GND, MODBUS.GND, DMX.GND, LED1.cathode
  N6: Компонент1.3V3, MODBUS.RE
  VCC: Компонент1.5V, MODBUS.VCC, DMX.VCC
  N7: Компонент1.D2_PWM, DMX.DE
  N8: Компонент1.D3_PWM, DMX.RE
  N9: Компонент1.D4_PWM, MODBUS.DE
  N10: MODBUS.A, J2.pin1
  N11: MODBUS.B, J2.pin2
  N12: DMX.A, J1.pin1
  N13: DMX.B, J1.pin2

notes:
  Принимаем сигнал по DMX и отправляем по MODBUS

custom parts:
  RS485 Module (MAX3485): Commercially available RS485 to RS232 TTL Module
